# Fritzing sketch micGrove (saved by Fritzing 0.9.3b)

parts:
  Shield = Base Shield V2
  Arduino = Arduino Uno (Rev3)  # not connected
  Sounds_Sensor = Grove Sound Sensor

nets:
  N1: Shield.pin_140, Sounds_Sensor.SIG
  N2: Shield.pin_141, Sounds_Sensor.NC
  N3: Shield.pin_142, Sounds_Sensor.VCC
  N4: Shield.pin_143, Sounds_Sensor.GND
