# Fritzing sketch brightness (saved by Fritzing 0.9.3b)
breadboards: 1

parts:
  Part1 = Arduino Uno (Rev3)
  Sensor = PHOTOCELL [package=photocell-kit]
  R2 = Resistor [tolerance=±5% resistance=220 package="0603 [SMD]"]

nets:
  N1: Part1.A0, Sensor.P$1, R2.Pin_0
  N2: Part1.GND, R2.Pin_1
  N3: Part1.5V, Sensor.P$2
