# Fritzing sketch brightnessGrove (saved by Fritzing 0.9.3b)

parts:
  Grove_Shield = Base Shield V2
  Arduino = Arduino Uno (Rev3)  # not connected
  Sensor = Grove Light Sensor

nets:
  N1: Grove_Shield.pin_140, Sensor.SIG
  N2: Grove_Shield.pin_141, Sensor.NC
  N3: Grove_Shield.pin_142, Sensor.VCC
  N4: Grove_Shield.pin_143, Sensor.GND

custom parts:
  Grove Light Sensor: An analog light sensor
