# Fritzing sketch rotationGrove (saved by Fritzing 0.9.3b)

parts:
  Grove_Shield = Base Shield V2
  Arduino = Arduino Uno (Rev3)  # not connected
  Rotary_Angle_Sesnor = Grove Rotary Angle Sensor

nets:
  N1: Grove_Shield.pin_140, Rotary_Angle_Sesnor.SIG
  N2: Grove_Shield.pin_141, Rotary_Angle_Sesnor.NC
  N3: Grove_Shield.pin_142, Rotary_Angle_Sesnor.VCC
  N4: Grove_Shield.pin_143, Rotary_Angle_Sesnor.GND

custom parts:
  Grove Rotary Angle Sensor: A potentiometer
