# Fritzing sketch noteGrove (saved by Fritzing 0.9.3b)

parts:
  Arduino = Arduino Uno (Rev3)  # not connected
  Shield = Base Shield V2
  Speaker = Grove Buzz

nets:
  N1: Shield.pin_140, Speaker.SIG
  N2: Shield.pin_141, Speaker.NC
  N3: Shield.pin_142, Speaker.VCC
  N4: Shield.pin_143, Speaker.GND

custom parts:
  Grove Buzz: A buzz
