# Fritzing sketch led (saved by Fritzing 0.9.3b)
breadboards: 1

parts:
  Part1 = Arduino Uno (Rev3)
  Sensor = PHOTOCELL [package=photocell-kit]
  R2 = Resistor [tolerance=±5% resistance=220 package="0603 [SMD]"]
  LED1 = LED - 3mm [color="Green (555nm)" package="3 mm [THT]"]

nets:
  N1: Part1.A0, Sensor.P$1, R2.Pin_0
  N2: Part1.D5_PWM, LED1.cathode
  N3: Part1.5V, Sensor.P$2, LED1.anode
  N4: Part1.GND, R2.Pin_1
