# Fritzing sketch ledGrove (saved by Fritzing 0.9.3b)

parts:
  Grove_Shield = Base Shield V2
  Arduino = Arduino Uno (Rev3)  # not connected
  Sensor = Grove Light Sensor
  LED = Grove LED

nets:
  N1: Grove_Shield.pin_108, LED.SIG
  N2: Grove_Shield.pin_109, LED.NC
  N3: Grove_Shield.pin_110, LED.VCC
  N4: Grove_Shield.pin_111, LED.GND
  N5: Grove_Shield.pin_140, Sensor.SIG
  N6: Grove_Shield.pin_141, Sensor.NC
  N7: Grove_Shield.pin_142, Sensor.VCC
  N8: Grove_Shield.pin_143, Sensor.GND

custom parts:
  Grove Light Sensor: An analog light sensor
  Grove LED: A light
