# Fritzing sketch fan (saved by Fritzing 0.9.3b)
breadboards: 1

parts:
  Part1 = Arduino Uno (Rev3)
  DC_Motor = DC Motor
  Rotary_Angle_Sensor = Rotary Potentiometer (Small) [maximum_resistance=100kΩ package=THT]

nets:
  N1: Part1.A0, Rotary_Angle_Sensor.wiper
  N2: Part1.D5_PWM, DC_Motor.pin_2
  N3: Part1.5V, DC_Motor.pin_1, Rotary_Angle_Sensor.leg1
  N4: Part1.GND, Rotary_Angle_Sensor.leg2
