# Fritzing sketch fanGrove (saved by Fritzing 0.9.3b)

parts:
  Arduino = Arduino Uno (Rev3)  # not connected
  Shield = Base Shield V2
  Rotary_Angle_Sensor = Grove Rotary Angle Sensor
  DC_Motor = DC Motor

nets:
  N1: Shield.pin_108, DC_Motor.pin_1
  N2: Shield.pin_111, DC_Motor.pin_2
  N3: Shield.pin_140, Rotary_Angle_Sensor.SIG
  N4: Shield.pin_141, Rotary_Angle_Sensor.NC
  N5: Shield.pin_142, Rotary_Angle_Sensor.VCC
  N6: Shield.pin_143, Rotary_Angle_Sensor.GND
  N7: Shield.pin_153, Shield.pin_155

custom parts:
  Grove Rotary Angle Sensor: A potentiometer
