# Fritzing sketch keyboard (saved by Fritzing 0.9.3b)
breadboards: 1

parts:
  Part1 = Arduino Uno (Rev3)
  S1 = Round Pushbutton
  S3 = Round Pushbutton
  Speaker = Piezo Speaker
  R1 = Resistor [tolerance=±5% resistance=220 package="2010 [SMD]"]
  R4 = Resistor [tolerance=±5% resistance=220 package="2010 [SMD]"]
  S4 = Round Pushbutton
  R5 = Resistor [tolerance=±5% resistance=220 package="2010 [SMD]"]

nets:
  N1: Part1.A0, Speaker.pin2
  N2: Part1.GND, S1.leg0, S3.leg0, Speaker.pin1, S4.leg0
  N3: Part1.D5_PWM, S3.leg1, R5.Pin_0
  N4: Part1.D6_PWM, R4.Pin_0, S4.leg1
  N5: Part1.D7, S1.leg1, R1.Pin_0
  N6: Part1.5V, R1.Pin_1, R4.Pin_1, R5.Pin_1

custom parts:
  Round Pushbutton: A generic pushbutton.
