# Fritzing sketch keyboardGrove (saved by Fritzing 0.9.3b)

parts:
  Arduino = Arduino Uno (Rev3)  # not connected
  Shield = Base Shield V2
  Speaker = Grove Button
  Button_1 = Grove Buzz
  Button_3 = Grove Button
  Button_2 = Grove Button

nets:
  N1: Shield.pin_108, Button_2.GND
  N2: Shield.pin_109, Button_2.VCC
  N3: Shield.pin_110, Button_2.NC
  N4: Shield.pin_111, Button_2.SIG
  N5: Shield.pin_112, Button_3.GND
  N6: Shield.pin_113, Button_3.VCC
  N7: Shield.pin_114, Button_3.NC
  N8: Shield.pin_115, Button_3.SIG
  N9: Shield.pin_116, Speaker.GND
  N10: Shield.pin_117, Speaker.VCC
  N11: Shield.pin_118, Speaker.NC
  N12: Shield.pin_119, Speaker.SIG
  N13: Shield.pin_140, Button_1.SIG
  N14: Shield.pin_141, Button_1.NC
  N15: Shield.pin_142, Button_1.VCC
  N16: Shield.pin_143, Button_1.GND

custom parts:
  Grove Buzz: A buzz
