# Fritzing sketch temp (saved by Fritzing 0.9.3b)
breadboards: 1

parts:
  Part1 = Arduino Uno (Rev3)
  Green = LED - 3mm [color="Green (555nm)" package="3 mm [THT]"]
  T3 = TMP36 Temperature Sensor [package="TO92 [THT]"]
  Red = LED - 3mm [color="Red (633nm)" package="3 mm [THT]"]

nets:
  N1: Part1.A0, T3.Vout
  N2: Part1.D6_PWM, Red.cathode
  N3: Part1.D7, Green.cathode
  N4: Part1.5V, T3.+Vs
  GND: Part1.GND, Green.anode, T3.GND, Red.anode
