# Fritzing sketch tempGrove (saved by Fritzing 0.9.3b)

parts:
  Arduino = Arduino Uno (Rev3)  # not connected
  Temp_Sensor = Grove Temperature Sensor
  Red_LED = Grove LED
  Green_LED = Grove LED
  Shield = Base Shield V2

nets:
  N1: Temp_Sensor.GND, Shield.pin_143
  N2: Temp_Sensor.VCC, Shield.pin_142
  N3: Temp_Sensor.SIG, Shield.pin_140
  N4: Temp_Sensor.NC, Shield.pin_141
  N5: Red_LED.GND, Shield.pin_116
  N6: Red_LED.VCC, Shield.pin_117
  N7: Red_LED.NC, Shield.pin_118
  N8: Red_LED.SIG, Shield.pin_119
  N9: Green_LED.GND, Shield.pin_112
  N10: Green_LED.VCC, Shield.pin_113
  N11: Green_LED.NC, Shield.pin_114
  N12: Green_LED.SIG, Shield.pin_115

custom parts:
  Grove Temperature Sensor: An analog temperature sensor
  Grove LED: A light
