# Fritzing sketch lights (saved by Fritzing 0.9.3b)
breadboards: 1

parts:
  Part1 = Arduino Uno (Rev3)
  LED1 = LED - 3mm [color="Red (633nm)" package="3 mm [THT]"]
  S2 = Round Pushbutton
  S5 = Round Pushbutton
  S6 = Round Pushbutton
  R1 = Resistor [tolerance=±5% resistance=220 package="0402 [SMD]"]
  R2 = Resistor [tolerance=±5% resistance=220 package="0402 [SMD]"]
  R3 = Resistor [tolerance=±5% resistance=220 package="0402 [SMD]"]
  LED2 = LED - 3mm [color="Yellow (585nm)" package="3 mm [THT]"]
  LED3 = LED - 3mm [color="Green (555nm)" package="3 mm [THT]"]

nets:
  N1: Part1.GND, LED1.anode, S2.leg1, S5.leg1, S6.leg1, LED2.anode, LED3.anode
  N2: Part1.D2, S2.leg0, R1.Pin_0
  N3: Part1.D3_PWM, S5.leg0, R2.Pin_0
  N4: Part1.D4, S6.leg0, R3.Pin_0
  N5: Part1.D5_PWM, LED1.cathode
  N6: Part1.D6_PWM, LED2.cathode
  N7: Part1.D7, LED3.cathode
  N8: Part1.5V, R1.Pin_1, R2.Pin_1, R3.Pin_1
