# Fritzing sketch lightsGrove (saved by Fritzing 0.9.3b)

parts:
  Grove_Shield = Base Shield V2
  Arduino = Arduino Uno (Rev3)  # not connected
  red_LED = Grove Button
  Yellow_LED = Grove Button
  Green_Button = Grove Button
  Red_Button = Grove LED
  Yellow_Button = Grove LED
  Green_LED = Grove LED

nets:
  N1: Grove_Shield.pin_96, Green_Button.GND
  N2: Grove_Shield.pin_97, Green_Button.VCC
  N3: Grove_Shield.pin_98, Green_Button.NC
  N4: Grove_Shield.pin_99, Green_Button.SIG
  N5: Grove_Shield.pin_100, Yellow_LED.GND
  N6: Grove_Shield.pin_101, Yellow_LED.VCC
  N7: Grove_Shield.pin_102, Yellow_LED.NC
  N8: Grove_Shield.pin_103, Yellow_LED.SIG
  N9: Grove_Shield.pin_104, red_LED.GND
  N10: Grove_Shield.pin_105, red_LED.VCC
  N11: Grove_Shield.pin_106, red_LED.NC
  N12: Grove_Shield.pin_107, red_LED.SIG
  N13: Grove_Shield.pin_108, Green_LED.GND
  N14: Grove_Shield.pin_109, Green_LED.VCC
  N15: Grove_Shield.pin_110, Green_LED.NC
  N16: Grove_Shield.pin_111, Green_LED.SIG
  N17: Grove_Shield.pin_112, Yellow_Button.GND
  N18: Grove_Shield.pin_113, Yellow_Button.VCC
  N19: Grove_Shield.pin_114, Yellow_Button.NC
  N20: Grove_Shield.pin_115, Yellow_Button.SIG
  N21: Grove_Shield.pin_116, Red_Button.GND
  N22: Grove_Shield.pin_117, Red_Button.VCC
  N23: Grove_Shield.pin_118, Red_Button.NC
  N24: Grove_Shield.pin_119, Red_Button.SIG

custom parts:
  Grove LED: A light
