# Fritzing sketch fanGrove (saved by Fritzing 0.9.3b)

parts:
  Arduino = Arduino Uno (Rev3)  # not connected
  Shield = Base Shield V2
  DC_Motor = DC Motor

nets:
  N1: Shield.pin_108, DC_Motor.pin_1
  N2: Shield.pin_111, DC_Motor.pin_2
  N3: Shield.pin_153, Shield.pin_155
