# Fritzing sketch noteGrove (saved by Fritzing 0.9.3b)

parts:
  Arduino = Arduino Uno (Rev3)  # not connected
  Shield = Base Shield V2
  Speaker = Grove Buzz

nets:
  N1: Shield.pin_108, Speaker.GND
  N2: Shield.pin_109, Speaker.VCC
  N3: Shield.pin_110, Speaker.NC
  N4: Shield.pin_111, Speaker.SIG

custom parts:
  Grove Buzz: A buzz
