# Fritzing sketch setTempGrove (saved by Fritzing 0.9.3b)

parts:
  Arduino = Arduino Uno (Rev3)  # not connected
  Shield = Base Shield V2
  Red = Grove LED
  Green = Grove LED

nets:
  N1: Shield.pin_112, Green.GND
  N2: Shield.pin_113, Green.VCC
  N3: Shield.pin_114, Green.NC
  N4: Shield.pin_115, Green.SIG
  N5: Shield.pin_116, Red.GND
  N6: Shield.pin_117, Red.VCC
  N7: Shield.pin_118, Red.NC
  N8: Shield.pin_119, Red.SIG

custom parts:
  Grove LED: A light
