# Fritzing sketch lights (saved by Fritzing 0.9.3b)
breadboards: 1

parts:
  Part1 = Arduino Uno (Rev3)
  LED1 = LED - 3mm [color="Red (633nm)" package="3 mm [THT]"]
  LED2 = LED - 3mm [color="Yellow (585nm)" package="3 mm [THT]"]
  LED3 = LED - 3mm [color="Green (555nm)" package="3 mm [THT]"]

nets:
  N1: Part1.D3_PWM, LED1.cathode
  N2: Part1.D5_PWM, LED2.cathode
  N3: Part1.D6_PWM, LED3.cathode
  N4: Part1.GND, LED1.anode, LED2.anode, LED3.anode
