# Fritzing sketch lightsGrove (saved by Fritzing 0.9.3b)

parts:
  Grove_Shield = Base Shield V2
  Arduino = Arduino Uno (Rev3)  # not connected
  Red = Grove LED
  Yellow = Grove LED
  Green = Grove LED

nets:
  N1: Grove_Shield.pin_100, Red.GND
  N2: Grove_Shield.pin_101, Red.VCC
  N3: Grove_Shield.pin_102, Red.NC
  N4: Grove_Shield.pin_103, Red.SIG
  N5: Grove_Shield.pin_108, Yellow.GND
  N6: Grove_Shield.pin_109, Yellow.VCC
  N7: Grove_Shield.pin_110, Yellow.NC
  N8: Grove_Shield.pin_111, Yellow.SIG
  N9: Grove_Shield.pin_112, Green.GND
  N10: Grove_Shield.pin_113, Green.VCC
  N11: Grove_Shield.pin_114, Green.NC
  N12: Grove_Shield.pin_115, Green.SIG

custom parts:
  Grove LED: A light
