# Fritzing sketch vary (saved by Fritzing 0.9.3b)
breadboards: 1

parts:
  Part1 = Arduino Uno (Rev3)
  Button = Round Pushbutton
  Motor = DC Motor
  R1 = Resistor [tolerance=±5% resistance=220 package="0402 [SMD]"]

nets:
  N1: Part1.D6_PWM, Motor.pin_2
  N2: Part1.D7, Button.leg0, R1.Pin_0
  N3: Part1.5V, R1.Pin_1
  N4: Part1.GND, Button.leg1, Motor.pin_1

custom parts:
  Round Pushbutton: A generic pushbutton.
