# Fritzing sketch varyGrove (saved by Fritzing 0.9.3b)

parts:
  Arduino = Arduino Uno (Rev3)  # not connected
  Shield = Base Shield V2
  Button = Grove Button
  DC_Motor = DC Motor

nets:
  N1: Shield.pin_112, DC_Motor.pin_1
  N2: Shield.pin_115, DC_Motor.pin_2
  N3: Shield.pin_116, Button.GND
  N4: Shield.pin_117, Button.VCC
  N5: Shield.pin_118, Button.NC
  N6: Shield.pin_119, Button.SIG
  N7: Shield.pin_153, Shield.pin_155
