# Fritzing sketch sounds (saved by Fritzing 0.9.3b)
breadboards: 1

parts:
  Part1 = Arduino Uno (Rev3)
  Speaker = Piezo Speaker
  R1 = Resistor [tolerance=±5% resistance=220 package="2512 [SMD]"]
  Button = Round Pushbutton

nets:
  N1: Part1.D5_PWM, Speaker.pin2
  N2: Part1.D7, R1.Pin_0, Button.leg1
  N3: Part1.5V, R1.Pin_1
  N4: Part1.GND, Speaker.pin1, Button.leg0

custom parts:
  Round Pushbutton: A generic pushbutton.
