# Fritzing sketch soundsGrove (saved by Fritzing 0.9.3b)

parts:
  Arduino = Arduino Uno (Rev3)  # not connected
  Grove_Shield = Base Shield V2
  Button = Grove Button
  Speaker = Grove Buzz

nets:
  N1: Grove_Shield.pin_100, Button.GND
  N2: Grove_Shield.pin_101, Button.VCC
  N3: Grove_Shield.pin_102, Button.NC
  N4: Grove_Shield.pin_103, Button.SIG
  N5: Grove_Shield.pin_116, Speaker.GND
  N6: Grove_Shield.pin_117, Speaker.VCC
  N7: Grove_Shield.pin_118, Speaker.NC
  N8: Grove_Shield.pin_119, Speaker.SIG

custom parts:
  Grove Buzz: A buzz
