# Fritzing sketch soundsGroveALT (saved by Fritzing 0.9.3b)

parts:
  Arduino = Arduino Uno (Rev3)  # not connected
  Grove_Shield = Base Shield V2
  Button = Grove Button
  Speaker = Piezo Speaker

nets:
  N1: Grove_Shield.pin_108, Speaker.pin1
  N2: Grove_Shield.pin_111, Speaker.pin2
  N3: Grove_Shield.pin_116, Button.GND
  N4: Grove_Shield.pin_117, Button.VCC
  N5: Grove_Shield.pin_118, Button.NC
  N6: Grove_Shield.pin_119, Button.SIG
