# Fritzing sketch temperatureGrove (saved by Fritzing 0.9.3b)

parts:
  Grove_Shield = Base Shield V2
  Temperature_Sensor = Grove Temperature Sensor
  Arduino = Arduino Uno (Rev3)  # not connected

nets:
  N1: Grove_Shield.pin_140, Temperature_Sensor.SIG
  N2: Grove_Shield.pin_141, Temperature_Sensor.NC
  N3: Grove_Shield.pin_142, Temperature_Sensor.VCC
  N4: Grove_Shield.pin_143, Temperature_Sensor.GND

custom parts:
  Grove Temperature Sensor: An analog temperature sensor
