# Fritzing sketch servoGrove (saved by Fritzing 0.9.3b)

parts:
  Arduino = Arduino Uno (Rev3)  # not connected
  Shield = Base Shield V2
  J1 = Basic Servo

nets:
  N1: Shield.pin_116, J1.gnd
  N2: Shield.pin_117, J1.vcc
  N3: Shield.pin_119, J1.pulse
