# Fritzing sketch volt (saved by Fritzing 0.9.3b)
breadboards: 1

parts:
  Part1 = Arduino Uno (Rev3)
  JP1 = M10X2 [package=2x10_lock]
  Part4 = 16x8 LED Matrix Backpack [part_number=2038]  # not connected
  Part5 = 16x8 LED Matrix Backpack [part_number=2038]  # not connected
  MIC1 = Microphone

nets:
  N1: Part1.A0, JP1.14
  N2: Part1.A1, JP1.13
  N3: Part1.A2, JP1.16
  N4: Part1.A3, JP1.15
  N5: Part1.A5/SCL, MIC1.pin2
  N6: Part1.D8, JP1.18
  N7: Part1.D9_PWM, JP1.20
  N8: Part1.D10_PWM/SS, JP1.17
  N9: Part1.D2, JP1.6
  N10: Part1.D3_PWM, JP1.3, JP1.4, JP1.5
  N11: Part1.D4, JP1.8
  N12: Part1.D5_PWM, JP1.10
  N13: Part1.D6_PWM, JP1.9
  N14: Part1.D7, JP1.12
  N15: Part1.GND, JP1.7, JP1.11, JP1.19, MIC1.pin1

custom parts:
  16x8 LED Matrix Backpack: This 16x8 monochrome LED matrix includes a driver chip for simple control via an I2C interface. The backpack features address-selection jumpers so you can connect up to eight matrices on a single I2C bus.
